# Fritzing sketch Circuit Diagram-Fritizing (saved by Fritzing 0.9.3b)
breadboards: 1

parts:
  Part1 = Arduino Uno (Rev3)
  Part2 = Rotoshield - Motor driver shield for Arduino
  M1 = DC Motor
  M2 = DC Motor
  M3 = DC Motor
  M4 = DC Motor
  Part3 = LIDAR-Lite
  VCC1 = Battery block 9V
  e-radionica1 = TCS230 Color Sensor [part_number=101209]

nets:
  N1: Part1.A0, Part2.A_IN_0
  N2: Part1.A1, Part2.A_IN_1
  N3: Part1.A2, Part2.A_IN_2
  N4: Part1.A3, Part2.A_IN_3
  N5: Part1.A4/SDA, Part2.A_IN_4
  N6: Part1.A5/SCL, Part2.A_IN_5
  N7: Part1.D8, Part2.DIG_8, e-radionica1.Out
  N8: Part1.D9_PWM, Part2.DIG_9
  N9: Part1.D10_PWM/SS, Part2.DIG_10
  N10: Part1.D11_PWM/MOSI, Part2.DIG_11
  N11: Part1.D12/MISO, Part2.DIG_12
  N12: Part1.D13/SCK, Part2.DIG_13
  GND: Part1.GND, Part2.GND, Part3.GND, VCC1.+, e-radionica1.Gnd
  N13: Part1.AREF, Part2.AREF
  N14: Part1.D0/RX, Part2.DIG_0
  N15: Part1.D1/TX, Part2.DIG_1
  N16: Part1.D2, Part2.DIG_2, Part3.SDA
  N17: Part1.D3_PWM, Part2.DIG_3, Part3.SCL
  N18: Part1.D4, Part2.DIG_4, e-radionica1.S0
  N19: Part1.D5_PWM, Part2.DIG_5, e-radionica1.S1
  N20: Part1.D6_PWM, Part2.DIG_6, e-radionica1.S2
  N21: Part1.D7, Part2.DIG_7, e-radionica1.S3
  N22: Part1.RESET, Part2.RESET
  3V3: Part1.3V3, Part2.+3V3
  5V: Part1.5V, Part3.5V, e-radionica1.Vcc
  VIN: Part1.VIN, Part2.VIN
  N23: Part2.M1-2, M3.pin_2
  N24: Part2.M1-1, M3.pin_1
  N25: Part2.M2-2, M4.pin_2
  N26: Part2.M2-1, M4.pin_1
  N27: Part2.M3-2, M1.pin_2
  N28: Part2.M3-1, M1.pin_1
  N29: Part2.M4-2, M2.pin_2
  N30: Part2.M4-1, M2.pin_1
  N31: Part2.VCC, VCC1.-

custom parts:
  LIDAR-Lite: PulsedLight LIDAR-Lite Sensor
  TCS230 Color Sensor: TCS230
